# Fritzing sketch bmp180 (saved by Fritzing 0.9.3b)

parts:
  BMP1 = BMP180
  Raspberry_Pi_1 = Raspberry Pi 3 [part_number=RPI-3-V1.2]

nets:
  VIN: BMP1.VIN, Raspberry_Pi_1.5V
  N1: BMP1.SCL, Raspberry_Pi_1.GPIO3
  N2: BMP1.SDA, Raspberry_Pi_1.GPIO2
  GND: BMP1.GND, Raspberry_Pi_1.GND
