# Fritzing sketch button-gpio4 (saved by Fritzing 0.9.3b)
breadboards: 1

parts:
  Raspberry_Pi_1 = Raspberry Pi 3 [part_number=RPI-3-V1.2]
  S1 = Pushbutton [package="[THT]"]
  R1 = Resistor [tolerance=±5% resistance=10k package=THT]

nets:
  N1: Raspberry_Pi_1.GPIO4, S1.Pin_3, S1.Pin_4, R1.Pin_1
  N2: Raspberry_Pi_1.GND, S1.Pin_1, S1.Pin_2
  N3: Raspberry_Pi_1.5V, R1.Pin_0
