# Fritzing sketch expander-PCF8575 (saved by Fritzing 0.9.3b)
breadboards: 1

parts:
  IC2 = PCF8575
  S1 = Pushbutton [package="[THT]"]
  R1 = Resistor [tolerance=±5% resistance=220 package=THT]
  LED1 = LED - 5mm [color="Red (633nm)" package="5 mm [THT]"]
  Raspberry_Pi_1 = Raspberry Pi 3 [part_number=RPI-3-V1.2]

nets:
  N1: IC2.GPB7, S1.Pin_3, S1.Pin_4, R1.Pin_1
  GND: IC2.GND, R1.Pin_0, LED1.cathode, Raspberry_Pi_1.GND
  3V3: IC2.VCC, S1.Pin_1, S1.Pin_2, Raspberry_Pi_1.3v3, Raspberry_Pi_1.3V3
  N2: IC2.SCL, Raspberry_Pi_1.GPIO3
  N3: IC2.SDA, Raspberry_Pi_1.GPIO2
  N4: IC2.GPA0, LED1.anode
