# Fritzing sketch expander-PCF8591-photoreistor (saved by Fritzing 0.9.3b)
breadboards: 1

parts:
  IC1 = Microchip PCF8591 4 Channel AD/DA expander [part_number=PCF8591 package="DIP (Dual Inline) [THT]"]
  Raspberry_Pi_1 = Raspberry Pi 3 [part_number=RPI-3-V1.2]
  R1 = Photocell (LDR) [package=THT]

nets:
  N1: IC1.AIN0, R1.pin_1
  VSS: IC1.A0, IC1.A1, IC1.A2, IC1.VSS, Raspberry_Pi_1.GND, R1.pin_0
  N2: IC1.SDA, Raspberry_Pi_1.GPIO2
  N3: IC1.SCL, Raspberry_Pi_1.GPIO3
  3V3: IC1.VREF, IC1.VDD, Raspberry_Pi_1.3v3, Raspberry_Pi_1.3V3
