# Fritzing sketch hmc5883l (saved by Fritzing 0.9.3b)

parts:
  パーツ1 = Triple Axis Magnetometer - HMC5883 Breakout
  Raspberry_Pi_1 = Raspberry Pi 3 [part_number=RPI-3-V1.2]

nets:
  GND: パーツ1.GND, Raspberry_Pi_1.GND
  VCC: パーツ1.VCC, Raspberry_Pi_1.5V
  N1: パーツ1.SDA, Raspberry_Pi_1.GPIO2
  N2: パーツ1.SCL, Raspberry_Pi_1.GPIO3
