# Fritzing sketch ir-motion (saved by Fritzing 0.9.3b)

parts:
  PIR1 = PIR sensor
  Raspberry_Pi_1 = Raspberry Pi 3 [part_number=RPI-3-V1.2]

nets:
  VDD: PIR1.VDD, Raspberry_Pi_1.5V
  N1: PIR1.SIG, Raspberry_Pi_1.GPIO23
  GND: PIR1.GND, Raspberry_Pi_1.GND

// code stored in the sketch: pir_sensor.ino
/* The sensor's output pin goes to HIGH if motion is present.
 * However, even if motion is present, it goes to LOW from time to time, 
 * which might give the impression no motion is present. 
 * This program deals with this issue by ignoring LOW-phases shorter than a given time, 
 * assuming continuous motion is present during these phases.
 *  
 */

/////////////////////////////
//VARS
int calibrationTime = 30; //the time we give the sensor to calibrate (10-60 secs according to the datasheet)       
long unsigned int lowIn;  //the time when the sensor outputs a low impulse
long unsigned int pause = 5000;  //the amount of milliseconds the sensor has to be low before we assume all motion has stopped

boolean lockLow = true;
boolean takeLowTime;  

int pirPin = 2;    //the digital pin connected to the PIR sensor's output
//int ledPin = 13;


/////////////////////////////
//SETUP
void setup(){
  Serial.begin(9600);
  pinMode(pirPin, INPUT);
  //pinMode(ledPin, OUTPUT);
  digitalWrite(pirPin, LOW); //No movement at the beginning

  //give the sensor some time to calibrate
  Serial.print("calibrating sensor ");
    for(int i = 0; i < calibrationTime; i++){
      Serial.print(".");
      delay(1000);
      }
    Serial.println(" done");
    Serial.println("SENSOR ACTIVE");
    delay(50);
  }

////////////////////////////
//LOOP
void loop(){

  if(digitalRead(pirPin) == HIGH){
      //digitalWrite(ledPin, HIGH);   //the led visualizes the sensors output pin state
      if(lockLow){  
         //makes sure we wait for a transition to LOW before any further output is made:
         lockLow = false;            
         Serial.println("---");
         Serial.print("motion detected at ");
         Serial.print(millis()/1000);
         Serial.println(" sec"); 
         delay(50);
         }         
       takeLowTime = true;
  }

  if(digitalRead(pirPin) == LOW){       
       //digitalWrite(ledPin, LOW);  //the led visualizes the sensors output pin state
       if(takeLowTime){
          lowIn = millis();          //save the time of the transition from high to LOW
          takeLowTime = false;       //make sure this is only done at the start of a LOW phase
       }
       //if the sensor is low for more than the given pause, 
       //we assume that no more motion is going to happen
       if(!lockLow && millis() - lowIn > pause){  
           //makes sure this block of code is only executed again after 
           //a new motion sequence has been detected
           lockLow = true;                        
           Serial.print("motion ended at ");      //output
           Serial.print((millis() - pause)/1000);
           Serial.println(" sec");
           delay(50);
       }
  }
}
