# Fritzing sketch lcd-parallel (saved by Fritzing 0.9.3b)
breadboards: 1

parts:
  LCD1 = LCD screen
  Raspberry_Pi_1 = Raspberry Pi 3 [part_number=RPI-3-V1.2]
  R1 = Trimmer Potentiometer [maximum_resistance=10kΩ package=THT]

nets:
  VSS: LCD1.VSS, LCD1.LED-, Raspberry_Pi_1.GND, R1.leg2
  VDD: LCD1.VDD, LCD1.R/W, LCD1.LED+, Raspberry_Pi_1.5V, R1.leg1
  N1: LCD1.V0, R1.wiper
  N2: LCD1.RS, Raspberry_Pi_1.GPIO21
  N3: LCD1.E, Raspberry_Pi_1.GPIO20
  N4: LCD1.DB4, Raspberry_Pi_1.GPIO8
  N5: LCD1.DB5, Raspberry_Pi_1.GPIO25
  N6: LCD1.DB6, Raspberry_Pi_1.GPIO24
  N7: LCD1.DB7, Raspberry_Pi_1.GPIO23
