# Fritzing sketch led-array (saved by Fritzing 0.9.3b)
breadboards: 1

parts:
  Raspberry_Pi_1 = Raspberry Pi 3 [part_number=RPI-3-V1.2]
  LED1 = LED - 5mm [color="Red (633nm)" package="5 mm [THT]"]
  LED2 = LED - 5mm [color="Green (570nm)" package="5 mm [THT]"]
  R1 = Resistor [tolerance=±5% resistance=220 package=THT]
  R2 = Resistor [tolerance=±5% resistance=220 package=THT]

nets:
  N1: Raspberry_Pi_1.GPIO13, R1.Pin_1
  N2: Raspberry_Pi_1.GPIO12, R2.Pin_1
  N3: Raspberry_Pi_1.GND, LED1.cathode, LED2.cathode
  N4: LED1.anode, R2.Pin_0
  N5: LED2.anode, R1.Pin_0
