# Fritzing sketch led-digits-HT16K33 (saved by Fritzing 0.9.3b)

parts:
  7SEG3 = 7-Segment LED I2C Backpack (white)
  Raspberry_Pi_1 = Raspberry Pi 3 [part_number=RPI-3-V1.2]

nets:
  N1: 7SEG3.V+, Raspberry_Pi_1.5V
  GND: 7SEG3.GND, Raspberry_Pi_1.GND
  N2: 7SEG3.SDA, Raspberry_Pi_1.GPIO2
  N3: 7SEG3.SCL, Raspberry_Pi_1.GPIO3

custom parts:
  7-Segment LED I2C Backpack (white): 4-digit, 7-segment LED Display with I2C Control
