# Fritzing sketch led-digits (saved by Fritzing 0.9.3b)

parts:
  U2 = MAX7219 [package=dil24]
  Raspberry_Pi_1 = Raspberry Pi 3 [part_number=RPI-3-V1.2]

nets:
  N1: U2.DIN, Raspberry_Pi_1.GPIO4
  N2: U2.CS, Raspberry_Pi_1.GPIO17
  N3: U2.CLK, Raspberry_Pi_1.GPIO27
  VCC: U2.VCC, Raspberry_Pi_1.5V
  GND: U2.GND, Raspberry_Pi_1.GND

custom parts:
  MAX7219: 8-digit, 8-segment LED display driver, serial input
