# Fritzing sketch led-matrix-HT16K33 (saved by Fritzing 0.9.3b)

parts:
  LED2 = 8x8 LED Matrix (yellow)
  Raspberry_Pi_1 = Raspberry Pi 3 [part_number=RPI-3-V1.2]

nets:
  N1: LED2.+, Raspberry_Pi_1.5V
  N2: LED2.-, Raspberry_Pi_1.GND
  N3: LED2.D, Raspberry_Pi_1.GPIO2
  N4: LED2.C, Raspberry_Pi_1.GPIO3

custom parts:
  8x8 LED Matrix (yellow): 8x8 LED Matrix with I2C control (yellow)
