# Fritzing sketch led-matrix (saved by Fritzing 0.9.3b)

parts:
  Part3 = LED Matrix - Serial Interface - Red/Green/Blue
  Raspberry_Pi_1 = Raspberry Pi 3 [part_number=RPI-3-V1.2]

nets:
  VCC: Part3.VCC, Raspberry_Pi_1.5V
  N1: Part3.SCK, Raspberry_Pi_1.GPIO17
  N2: Part3.CS, Raspberry_Pi_1.GPIO27
  N3: Part3.MISO, Raspberry_Pi_1.GPIO4
  GND: Part3.GND, Raspberry_Pi_1.GND
