# Fritzing sketch led-rgb-anode (saved by Fritzing 0.9.3b)
breadboards: 1

parts:
  Raspberry_Pi_1 = Raspberry Pi 3 [part_number=RPI-3-V1.2]
  R1 = Resistor [tolerance=±5% resistance=220 package=THT]
  R2 = Resistor [tolerance=±5% resistance=220 package=THT]
  R3 = Resistor [tolerance=±5% resistance=220 package=THT]
  LED1 = RGB LED - (4 legs) [package="5 mm [THT]"]

nets:
  N1: Raspberry_Pi_1.GPIO13, R3.Pin_1
  N2: Raspberry_Pi_1.GPIO12, R2.Pin_1
  N3: Raspberry_Pi_1.GPIO18, R1.Pin_1
  N4: Raspberry_Pi_1.5V, LED1.common_anode
  N5: R1.Pin_0, LED1.red_cathode
  N6: R2.Pin_0, LED1.green_cathode
  N7: R3.Pin_0, LED1.blue_cathode
