# Fritzing sketch led-rgb (saved by Fritzing 0.9.3b)
breadboards: 1

parts:
  Raspberry_Pi_1 = Raspberry Pi 3 [part_number=RPI-3-V1.2]
  LED1 = RGB LED (com. cathode, rgb) [package="5 mm [THT]"]
  R1 = Resistor [tolerance=±5% resistance=220 package=THT]
  R2 = Resistor [tolerance=±5% resistance=220 package=THT]
  R3 = Resistor [tolerance=±5% resistance=220 package=THT]

nets:
  N1: Raspberry_Pi_1.GPIO13, R3.Pin_1
  N2: Raspberry_Pi_1.GPIO12, R2.Pin_1
  N3: Raspberry_Pi_1.GND, LED1.common_cathode
  N4: Raspberry_Pi_1.GPIO18, R1.Pin_1
  N5: LED1.red_anode, R1.Pin_0
  N6: LED1.green_anode, R2.Pin_0
  N7: LED1.blue_anode, R3.Pin_0
