# Fritzing sketch mpu6050 (saved by Fritzing 0.9.3b)

parts:
  GY1 = MPU-6050 Board GY-521 [form="♀ (female)" package=THT]
  Raspberry_Pi_1 = Raspberry Pi 3 [part_number=RPI-3-V1.2]

nets:
  3V3: GY1.pin1, Raspberry_Pi_1.3v3, Raspberry_Pi_1.3V3
  N1: GY1.pin2, Raspberry_Pi_1.GND
  N2: GY1.pin3, Raspberry_Pi_1.GPIO3
  N3: GY1.pin4, Raspberry_Pi_1.GPIO2

custom parts:
  MPU-6050 Board GY-521: Acelerometro y Giroscopio MPU-6050 Board GY-521
