# Fritzing sketch relay-no (saved by Fritzing 0.9.3b)

parts:
  Power_plug1 = Power plug
  U2 = V18ZA2P [package=v18za2p]
  KY-1 = Keyes Relay [package=THT]
  Raspberry_Pi_1 = Raspberry Pi 3 [part_number=RPI-3-V1.2]

nets:
  N1: Power_plug1.GND, U2.-
  N2: Power_plug1.VCC, KY-1.C
  N3: U2.+, KY-1.NC
  N4: KY-1.signal, Raspberry_Pi_1.GPIO23
  N5: KY-1.power, Raspberry_Pi_1.5V
  N6: KY-1.ground, Raspberry_Pi_1.GND

custom parts:
  V18ZA2P: Varistor
  Keyes Relay: The Keyes 5V relay module is suitable for SCM development, home appliance control. It uses a 5V~12V TIL control signal which can control DC / AC signal.
