# Fritzing sketch servo-PCA9685 (saved by Fritzing 0.9.3b)

parts:
  Part3 = 16-Channel 12-bit PCA9685 PWM/Servo Driver
  J1 = Screw terminal - 2 pins [package=THT]
  Power_plug1 = Power plug
  J2 = Basic Servo
  Raspberry_Pi_1 = Raspberry Pi 3 [part_number=RPI-3-V1.2]

nets:
  N1: Part3.PWRIN, J1.pin1, Power_plug1.VCC
  GND: Part3.GND, J1.pin2, Power_plug1.GND, J2.gnd, Raspberry_Pi_1.GND
  N2: Part3.0, J2.pulse
  N3: Part3.V+, J2.vcc
  VCC: Part3.VCC, Raspberry_Pi_1.5V
  N4: Part3.SDA, Raspberry_Pi_1.GPIO2
  N5: Part3.SCL, Raspberry_Pi_1.GPIO3

custom parts:
  16-Channel 12-bit PCA9685 PWM/Servo Driver: The Adafruit 16-Channel 12-bit PWM/Servo Driver will drive up to 16 servos over I2C with only 2 pins. The on-board PCA9685 PWM controller will drive all 16 channels simultaneously with no additional processing overhead. What's more, you can chain up to 62 of them to control up to 992 servos - all with the same 2 pins
