# Fritzing sketch shift-register-7seg-anodo (saved by Fritzing 0.9.3b)
breadboards: 1

parts:
  DI1 = 7-Segment LED Display [package=THT]
  U1 = 74HC595 [package="DIP16 [THT]"]
  Raspberry_Pi_1 = Raspberry Pi 3 [part_number=RPI-3-V1.2]
  R1 = Resistor [tolerance=±5% resistance=220 package=THT]

nets:
  N1: DI1.cathodeE, U1.Q4
  N2: DI1.cathodeD, U1.Q3
  N3: DI1.commAnode#2, R1.Pin_0
  N4: DI1.cathodeC, U1.Q2
  N5: DI1.cathodeDP, U1.Q7
  N6: DI1.cathodeB, U1.Q1
  N7: DI1.cathodeA, U1.Q0
  N8: DI1.cathodeF, U1.Q5
  N9: DI1.cathodeG, U1.Q6
  GND: U1.GND, U1.OE, Raspberry_Pi_1.GND
  VCC: U1.MR, U1.VCC, Raspberry_Pi_1.3v3, R1.Pin_1
  N10: U1.SH_CP, Raspberry_Pi_1.GPIO17
  N11: U1.ST_CP, Raspberry_Pi_1.GPIO27
  N12: U1.DS, Raspberry_Pi_1.GPIO4
