# Fritzing sketch shift-register (saved by Fritzing 0.9.3b)
breadboards: 1

parts:
  U1 = 74HC595 [package="DIP16 [THT]"]
  LED1 = LED - 5mm [color="Red (633nm)" package="5 mm [THT]"]
  LED2 = LED - 5mm [color="Red (633nm)" package="5 mm [THT]"]
  LED3 = LED - 5mm [color="Red (633nm)" package="5 mm [THT]"]
  LED4 = LED - 5mm [color="Red (633nm)" package="5 mm [THT]"]
  LED5 = LED - 5mm [color="Red (633nm)" package="5 mm [THT]"]
  LED6 = LED - 5mm [color="Red (633nm)" package="5 mm [THT]"]
  LED7 = LED - 5mm [color="Red (633nm)" package="5 mm [THT]"]
  LED8 = LED - 5mm [color="Red (633nm)" package="5 mm [THT]"]
  R1 = Resistor [tolerance=±5% resistance=220 package=THT]
  R2 = Resistor [tolerance=±5% resistance=220 package=THT]
  R3 = Resistor [tolerance=±5% resistance=220 package=THT]
  R4 = Resistor [tolerance=±5% resistance=220 package=THT]
  R5 = Resistor [tolerance=±5% resistance=220 package=THT]
  R6 = Resistor [tolerance=±5% resistance=220 package=THT]
  R7 = Resistor [tolerance=±5% resistance=220 package=THT]
  R8 = Resistor [tolerance=±5% resistance=220 package=THT]
  Raspberry_Pi_1 = Raspberry Pi 3 [part_number=RPI-3-V1.2]

nets:
  N1: U1.Q1, R7.Pin_1
  N2: U1.Q2, R6.Pin_1
  N3: U1.Q3, R5.Pin_1
  N4: U1.Q4, R4.Pin_1
  N5: U1.Q5, R3.Pin_1
  N6: U1.Q6, R2.Pin_1
  N7: U1.Q7, R1.Pin_1
  GND: U1.GND, U1.OE, LED1.cathode, LED2.cathode, LED3.cathode, LED4.cathode, LED5.cathode, LED6.cathode, LED7.cathode, LED8.cathode, Raspberry_Pi_1.GND
  VCC: U1.MR, U1.VCC, Raspberry_Pi_1.3v3
  N8: U1.SH_CP, Raspberry_Pi_1.GPIO17
  N9: U1.ST_CP, Raspberry_Pi_1.GPIO27
  N10: U1.DS, Raspberry_Pi_1.GPIO4
  N11: U1.Q0, R8.Pin_0
  N12: LED1.anode, R1.Pin_0
  N13: LED2.anode, R2.Pin_0
  N14: LED3.anode, R3.Pin_0
  N15: LED4.anode, R4.Pin_0
  N16: LED5.anode, R5.Pin_0
  N17: LED6.anode, R6.Pin_0
  N18: LED7.anode, R7.Pin_0
  N19: LED8.anode, R8.Pin_1
