# Fritzing sketch switch-nc (saved by Fritzing 0.9.3b)
breadboards: 1

parts:
  Raspberry_Pi_1 = Raspberry Pi 3 [part_number=RPI-3-V1.2]
  S1 = Toggle Switch [package=THT]
  R1 = Resistor [tolerance=±5% resistance=220 package=THT]

nets:
  N1: Raspberry_Pi_1.3v3, S1.L1
  N2: Raspberry_Pi_1.GND, R1.Pin_1
  N3: Raspberry_Pi_1.GPIO23, S1.COM, R1.Pin_0
